# Fritzing sketch drawer_sketch (saved by Fritzing 0.7.12b)
breadboards: 1

parts:
  Arduino1 = Arduino
  J1 = Basic Servo
  J2 = Infrared Proximity Sensor
  IC1 = IC, DIP package, 16 pins [chip_label=IC]
  M1 = DC Motor
  M2 = DC Motor
  R3 = Resistor [tolerance=±5% resistance=10k package=THT]
  R4 = Resistor [tolerance=±5% resistance=10k package=THT]
  R5 = Photocell (LDR) [package=THT]
  R6 = Photocell (LDR) [package=THT]

nets:
  N1: Arduino1.A0, J2.Vout
  N2: Arduino1.A1, J1.pulse
  N3: Arduino1.A4, R3.Pin_1, R5.pin_0
  N4: IC1.pin3, M2.pin_2
  N5: IC1.pin4, IC1.pin5, IC1.pin12, IC1.pin13
  N6: IC1.pin6, M2.pin_1
  N7: IC1.pin8, IC1.pin16
  N8: IC1.pin11, M1.pin_2
  N9: IC1.pin14, M1.pin_1
  N10: R3.Pin_0, R4.Pin_0
  N11: R4.Pin_1, R6.pin_0
  N12: R5.pin_1, R6.pin_1
